# Fritzing sketch nucleo_led (saved by Fritzing 1.0.5)
breadboards: 1

parts:
  R1 = Resistor [tolerance=±5% power=0.25W resistance=110 package=THT]
  J1 = STM32 Nucleo boards
  R2 = Resistor [tolerance=±5% power=0.25W resistance=110 package=THT]
  R3 = Resistor [tolerance=±5% power=0.25W resistance=110 package=THT]
  R4 = Resistor [tolerance=±5% power=0.25W resistance=110 package=THT]
  R5 = Resistor [tolerance=±5% power=0.25W resistance=110 package=THT]
  R6 = Resistor [tolerance=±5% power=0.25W resistance=110 package=THT]
  R7 = Resistor [tolerance=±5% power=0.25W resistance=110 package=THT]
  R8 = Resistor [tolerance=±5% power=0.25W resistance=110 package=THT]
  LED1 = LED - 3mm [color="Green (555nm)" current=0.030A package="3 mm [THT]"]
  LED2 = LED - 3mm [color="Green (555nm)" current=0.030A package="3 mm [THT]"]
  LED3 = LED - 3mm [color="Green (555nm)" current=0.030A package="3 mm [THT]"]
  LED4 = LED - 3mm [color="Green (555nm)" current=0.030A package="3 mm [THT]"]
  LED5 = LED - 3mm [color="Green (555nm)" current=0.030A package="3 mm [THT]"]
  LED6 = LED - 3mm [color="Green (555nm)" current=0.030A package="3 mm [THT]"]
  LED7 = LED - 3mm [color="Green (555nm)" current=0.030A package="3 mm [THT]"]
  LED8 = LED - 3mm [color="Green (555nm)" current=0.030A package="3 mm [THT]"]

nets:
  N1: R1.Pin_0, LED1.cathode
  N2: R1.Pin_1, J1.GND, R2.Pin_1, R3.Pin_1, R4.Pin_1, R5.Pin_1, R6.Pin_1, R7.Pin_1, R8.Pin_1
  N3: J1.D8, LED7.anode
  N4: J1.D9_PWM, LED8.anode
  N5: J1.D2, LED1.anode
  N6: J1.D3_PWM, LED2.anode
  N7: J1.D4, LED3.anode
  N8: J1.D5_PWM, LED4.anode
  N9: J1.D6_PWM, LED5.anode
  N10: J1.D7, LED6.anode
  N11: R2.Pin_0, LED2.cathode
  N12: R3.Pin_0, LED3.cathode
  N13: R4.Pin_0, LED4.cathode
  N14: R5.Pin_0, LED5.cathode
  N15: R6.Pin_0, LED6.cathode
  N16: R7.Pin_0, LED7.cathode
  N17: R8.Pin_0, LED8.cathode
