# Fritzing sketch nucleo_7seg_display (saved by Fritzing 1.0.6)
breadboards: 1

parts:
  R1 = Resistor [tolerance=±5% power=0.25W resistance=110 package=THT]
  J1 = STM32 Nucleo boards
  R2 = Resistor [tolerance=±5% power=0.25W resistance=110 package=THT]
  R3 = Resistor [tolerance=±5% power=0.25W resistance=110 package=THT]
  R4 = Resistor [tolerance=±5% power=0.25W resistance=110 package=THT]
  R5 = Resistor [tolerance=±5% power=0.25W resistance=110 package=THT]
  R6 = Resistor [tolerance=±5% power=0.25W resistance=110 package=THT]
  R7 = Resistor [tolerance=±5% power=0.25W resistance=110 package=THT]
  R8 = Resistor [tolerance=±5% power=0.25W resistance=110 package=THT]
  LED9 = 7-SEGMENT-4DIGIT-YOUNGSUN [package=7-segment-4digit-youngsun-longpads]  # not connected
  Q1 = PNP-Transistor [part_number=BC640 package="TO92 [THT]"]
  Q2 = PNP-Transistor [part_number=BC640 package="TO92 [THT]"]
  Q3 = PNP-Transistor [part_number=BC640 package="TO92 [THT]"]
  Q4 = PNP-Transistor [part_number=BC640 package="TO92 [THT]"]

nets:
  N1: R1.Pin_0, Q1.B
  N2: R1.Pin_1, J1.A4/SDA
  N3: J1.D10_PWM/SS, R4.Pin_1
  N4: J1.D11_PWM/MOSI, R3.Pin_1
  N5: J1.D12/MISO, R2.Pin_1
  N6: J1.3V3, Q1.E, Q2.E, Q3.E, Q4.E
  N7: R2.Pin_0, Q2.B
  N8: R3.Pin_0, Q3.B
  N9: R4.Pin_0, Q4.B
  N10: R5.Pin_1, Q1.C
  N11: R6.Pin_0, Q2.C
  N12: R7.Pin_1, Q3.C
  N13: R8.Pin_1, Q4.C
