# Fritzing sketch esp32-wroom-32d_devkit_c (saved by Fritzing 1.0.7)
breadboards: 2

parts:
  U1 = ESP32-WROOM-32D-NodeMCU
  U2 = MAX485 [package=dil08]
  R1 = Resistor [tolerance=±5% resistance=100 package="1206 [SMD]"]
  R2 = Resistor [tolerance=±5% resistance=220 package="1206 [SMD]"]
  LED1 = LED - 3mm [color="Green (560nm)" current=0.030A package="3 mm [THT]"]

nets:
  3.3V: U1.3.3V, U2.VCC
  N1: U1.G35, U1.G13, U1.CLK
  N2: U1.G32, U1.GND#13, U1.SD3, U1.SD0, U2.GND
  N3: U1.G15, U2.RE, U2.DE
  N4: U1.G2, R2.Pin_0
  N5: U1.G16, U2.RO
  N6: U1.G17, U2.DI
  N7: U1.GND#44, LED1.cathode
  N8: U2.A, R1.Pin_1
  N9: U2.B, R1.Pin_0
  N10: R2.Pin_1, LED1.anode

notes:
  3.3V transceiver needed instead of MAX485: ADM3485E or SN65HVD12
  RS-485 B A
