# Fritzing sketch wemos-s2-mini (saved by Fritzing 1.0.7)
breadboards: 1

parts:
  U2 = MAX485 [package=dil08]
  R1 = Resistor [tolerance=±5% resistance=100 package="1206 [SMD]"]
  A1 = Wemos S2 Mini [part_number="WeMos D1 Mini Lite"]

nets:
  N1: U2.RO, A1.Pin_20
  N2: U2.RE, U2.DE
  N3: U2.DI, A1.Pin_27
  N4: U2.GND, A1.Pin_18, A1.Pin_26
  N5: U2.A, R1.Pin_1
  N6: U2.B, R1.Pin_0
  N7: U2.VCC, A1.Pin_8

notes:
  3.3V transceiver needed instead of MAX485: ADM3485E or SN65HVD12
  RS-485 B A

custom parts:
  Wemos S2 Mini: A mini wifi board based on the ESP32-S2FN4R2.
