# Fritzing sketch wemos-s2-mini_ir_transmitter (saved by Fritzing 1.0.7)
breadboards: 1

parts:
  A1 = Wemos S2 Mini [part_number="WeMos D1 Mini Lite"]
  R1 = Resistor [tolerance=±5% resistance=47 package="1206 [SMD]"]
  R2 = Resistor [tolerance=±5% resistance=1k package="1206 [SMD]"]
  U1 = TRANSISTOR_NPN_2 [part_number=BC337 package=to-92]
  LED1 = LED - 5mm [color="Infrared (940nm)" current=0.030A package="5 mm [THT]"]

nets:
  N1: A1.Pin_1, A1.Pin_9
  N2: A1.Pin_2, A1.Pin_10
  N3: A1.Pin_3, A1.Pin_11
  N4: A1.Pin_4, A1.Pin_12
  N5: A1.Pin_5, A1.Pin_13
  N6: A1.Pin_6, A1.Pin_14
  N7: A1.Pin_7, A1.Pin_15
  N8: A1.Pin_8, A1.Pin_16
  N9: A1.Pin_17, A1.Pin_25, R1.Pin_0
  N10: A1.Pin_18, A1.Pin_26, U1.E
  N11: A1.Pin_19, A1.Pin_27
  N12: A1.Pin_20, A1.Pin_28
  N13: A1.Pin_21, A1.Pin_29, R2.Pin_1
  N14: A1.Pin_22, A1.Pin_30
  N15: A1.Pin_23, A1.Pin_31
  N16: A1.Pin_24, A1.Pin_32
  N17: R1.Pin_1, LED1.anode
  N18: R2.Pin_0, U1.B
  N19: U1.C, LED1.cathode

custom parts:
  Wemos S2 Mini: A mini wifi board based on the ESP32-S2FN4R2.
